// Logisim project read_cache.circ as structural Verilog: 3 circuits, main circuit AssocCache
module AssocCache (
  input  [15:0] address,
  input  Clear,
  input  Clock,
  output [15:0] data_out,
  output Hit,
  output Stallable_Clock
);

  wire adder_1_cout, adder_2_cout, and_1_out, and_2_out, comparator_1_eq, comparator_2_eq, comparator_3_lt,
       hit_t, memory_1_first, memory_1_stalled, not_1_out, not_2_out, not_3_out, not_4_out, or_2_out,
       Way0_Store_Mem, Way1_Store_Mem;
  wire [3:0] adder_1_out, adder_2_out, multiplexer_2_out, multiplexer_5_out, ram_2_data;
  wire [15:0] ram_1_data_2;
  wire [26:11] mem_block;
  wire [27:0] ram_2_data_2;
  wire [31:0] multiplexer_1_out, multiplexer_4_out, ram_1_data;
  wire [31:28] multiplexer_3_out, multiplexer_6_out;

  RAM #(.addrWidth(5), .dataWidth(32), .bus("separate")) ram_1 (
    .addr(address[4:0]), .din(multiplexer_1_out), .data({ram_1_data[31:27], ram_1_data_2, ram_1_data[10:0]}),
    .str(or_2_out), .sel(1'b1), .clk(Clock), .ld(1'b1), .clr(Clear));
  Comparator #(.width(11)) comparator_1 (
    .a(ram_1_data[10:0]), .b(address[15:5]), .eq(comparator_1_eq));  // open: gt, lt
  Multiplexer #(.width(32), .enable("false")) multiplexer_1 (
    .in0({multiplexer_3_out, ram_1_data[27], ram_1_data_2, ram_1_data[10:0]}),
    .in1({5'b00001, mem_block, address[15:5]}), .out(multiplexer_1_out), .sel(Way0_Store_Mem));
  Adder #(.width(4)) adder_1 (.a(4'b0001), .b(ram_1_data[31:28]), .out(adder_1_out), .cout(adder_1_cout));  // open: cin
  Multiplexer #(.width(4), .disabled(0), .enable("false")) multiplexer_2 (
    .in0(adder_1_out), .in1(4'b0011), .out(multiplexer_2_out), .sel(adder_1_cout));
  and and_1 (and_1_out, ram_1_data[27], comparator_1_eq);
  Multiplexer #(.width(4), .disabled(0), .enable("false")) multiplexer_3 (
    .in0(multiplexer_2_out), .in1(4'b0000), .out(multiplexer_3_out), .sel(and_1_out));
  LED led_1 (.in(and_1_out));
  or or_1 (hit_t, and_2_out, and_1_out);
  or or_2 (or_2_out, not_4_out, hit_t);
  Memory memory_1 (
    .Address(address), .store(1'b0), .select(not_1_out), .clear(Clear), .clock(Clock), .data_out(mem_block),
    .stalleable_clock(Stallable_Clock), .Stalled(memory_1_stalled), .First(memory_1_first));  // open: data_in
  Hex_Digit_Display hex_digit_display_1 (.value(ram_1_data[31:28]));  // open: dp
  LED led_2 (.in(memory_1_stalled));
  Hex_Digit_Display hex_digit_display_2 (.value(ram_2_data));  // open: dp
  RAM #(.addrWidth(5), .dataWidth(32), .bus("separate")) ram_2 (
    .addr(address[4:0]), .din(multiplexer_4_out), .data({ram_2_data, ram_2_data_2}), .str(or_2_out),
    .sel(1'b1), .clk(Clock), .ld(1'b1), .clr(Clear));
  Comparator #(.width(11)) comparator_2 (
    .a(ram_2_data_2[10:0]), .b(address[15:5]), .eq(comparator_2_eq));  // open: gt, lt
  not not_1 (not_1_out, hit_t);
  Comparator #(.width(4), .mode("unsigned")) comparator_3 (
    .a(ram_1_data[31:28]), .b(ram_2_data), .lt(comparator_3_lt));  // open: gt, eq
  Multiplexer #(.width(32), .enable("false")) multiplexer_4 (
    .in0({multiplexer_6_out, ram_2_data_2}), .in1({5'b00001, mem_block, address[15:5]}),
    .out(multiplexer_4_out), .sel(Way1_Store_Mem));
  and and_2 (and_2_out, ram_2_data_2[27], comparator_2_eq);
  Multiplexer #(.width(4), .disabled(0), .enable("false")) multiplexer_5 (
    .in0(adder_2_out), .in1(4'b0011), .out(multiplexer_5_out), .sel(adder_2_cout));
  Adder #(.width(4)) adder_2 (.a(4'b0001), .b(ram_2_data), .out(adder_2_out), .cout(adder_2_cout));  // open: cin
  not not_2 (not_2_out, hit_t);
  not not_3 (not_3_out, comparator_3_lt);
  Multiplexer #(.width(4), .disabled(0), .enable("false")) multiplexer_6 (
    .in0(multiplexer_5_out), .in1(4'b0000), .out(multiplexer_6_out), .sel(and_2_out));
  LED led_3 (.in(and_2_out));
  not not_4 (not_4_out, memory_1_stalled);
  and and_3 (Way0_Store_Mem, not_2_out, not_3_out);
  and and_4 (Way1_Store_Mem, not_2_out, comparator_3_lt);
  assign data_out = and_1_out ? ram_1_data_2 : 16'bz;  // Controlled_Buffer controlled_buffer_1
  assign data_out = and_2_out ? ram_2_data_2[26:11] : 16'bz;  // Controlled_Buffer controlled_buffer_2
  assign data_out = not_1_out ? mem_block : 16'bz;  // Controlled_Buffer controlled_buffer_3
  and and_5 (Hit, hit_t, memory_1_first);
  LED led_4 (.in(or_2_out));
  LED led_5 (.in(not_4_out));

  // Other names for the same wires on the sheet: clr = Clear; mem_block[10:0] = address[15:5];
  //   req_tag[10:0] = address[15:5]; mem_data[15:0] = mem_block

  // Notes on the sheet:
  //   input address from CPU
  //   index
  //   tag
  //   Way0
  //   0-4: tag
  //   5-20: data
  //   21: valid
  //   20-23: LRU
  //   tag
  //   data
  //   valid
  //   age
  //   Saturating Cntr
  //   way0 hit
  //   Way1
  //   Memory
  //   Way0 Age 
  //   tag
  //   data
  //   valid
  //   age
  //   stalled
  //   Way1 Age 
  //   pick oldest way to be replaced on miss
  //   Saturating Cntr
  //   way1 hit
  //   Form a new line to fill cache with data, tag, valid bit and LRU age to zero
  //   return data ready
  //   data return ready
endmodule

module Memory (
  input  [15:0] Address,
  input  [15:0] data_in,
  input  store,
  input  select,
  input  clear,
  input  clock,
  output [15:0] data_out,
  output stalleable_clock,
  output Stalled,
  output First
);

  wire counter_1_carry, or_1_out;
  wire [7:0] counter_1_q, register_1_q;

  or or_1 (or_1_out, store, select);
  RAM #(.addrWidth(16), .dataWidth(16), .bus("separate")) ram_1 (
    .addr(Address), .din(data_in), .data(data_out), .str(store), .sel(1'b1), .clk(stalleable_clock),
    .ld(select), .clr(1'b0));
  Counter #(.max('ha)) counter_1 (
    .count(or_1_out), .Q(counter_1_q), .carry(counter_1_carry), .clk(clock), .clr(clear));  // open: load, D
  Hex_Digit_Display hex_digit_display_1 (.value(counter_1_q[7:4]));  // open: dp
  or or_2 (stalleable_clock, clock, or_1_out, counter_1_carry);
  Hex_Digit_Display hex_digit_display_2 (.value(counter_1_q[3:0]));  // open: dp
  Register register_1 (.D(counter_1_q), .Q(register_1_q), .clk(clock));  // open: en, clr
  and and_1 (Stalled, select, ~counter_1_carry);  // AND_Gate
  Comparator comparator_1 (.a(register_1_q), .b({8{1'b0}}), .eq(First));  // open: gt, lt

  // Notes on the sheet:
  //   Main Memory
  //   delay counter
  //   last cntr
endmodule

module Main (
);

  wire and_1_out, assoccache_1_hit, assoccache_1_stallable_clock, button_1_out, clock_1_out, counter_1_carry,
       or_1_out;
  wire [7:0] counter_2_q;
  wire [15:0] adder_1_out, assoccache_1_data_out, counter_1_q, ram_1_data;

  Counter #(.width(16), .max('h3f), .ongoal("stay")) counter_1 (
    .Q(counter_1_q), .carry(counter_1_carry), .clk(or_1_out), .clr(button_1_out));  // open: load, D, count
  or or_1 (or_1_out, counter_1_carry, assoccache_1_stallable_clock);
  Button button_1 (.out(button_1_out));
  Adder #(.width(16)) adder_1 (.a(counter_1_q), .b(16'h1), .out(adder_1_out));  // open: cin, cout
  LED led_1 (.in(counter_1_carry));
  Hex_Digit_Display hex_digit_display_1 (.value(adder_1_out[3:0]), .dp(1'b0));
  Hex_Digit_Display hex_digit_display_2 (.value(adder_1_out[7:4]), .dp(1'b0));
  RAM #(.addrWidth(16), .bus("separate")) ram_1 (
    .addr(counter_1_q), .data(ram_1_data[7:0]), .sel(1'b1), .ld(1'b1), .clr(1'b0));  // open: din, str, clk
  Clock clock_1 (.out(clock_1_out));
  AssocCache assoccache_1 (
    .address(ram_1_data), .Clear(button_1_out), .Clock(clock_1_out), .data_out(assoccache_1_data_out),
    .Hit(assoccache_1_hit), .Stallable_Clock(assoccache_1_stallable_clock));
  Counter counter_2 (
    .count(and_1_out), .Q(counter_2_q), .clk(clock_1_out), .clr(button_1_out));  // open: load, D, carry
  Hex_Digit_Display hex_digit_display_3 (.value(assoccache_1_data_out[3:0]), .dp(1'b0));
  Hex_Digit_Display hex_digit_display_4 (.value(counter_2_q[7:4]), .dp(1'b0));
  Hex_Digit_Display hex_digit_display_5 (.value(assoccache_1_data_out[7:4]), .dp(1'b0));
  Hex_Digit_Display hex_digit_display_6 (.value(assoccache_1_data_out[11:8]), .dp(1'b0));
  LED led_2 (.in(and_1_out));
  and and_1 (and_1_out, assoccache_1_hit, ~counter_1_carry);  // AND_Gate
  Hex_Digit_Display hex_digit_display_7 (.value(counter_2_q[3:0]), .dp(1'b0));
  Hex_Digit_Display hex_digit_display_8 (.value(assoccache_1_data_out[15:12]), .dp(1'b0));
  // Pins of 8 and 16 bits meet at ram_1_data

  // Notes on the sheet:
  //   Clear
  //   Sequence Counter
  //   Request Count
  //   Address Sequence 
  //   DONE
  //   Data Values
  //   Hit Count
  //   HIT
endmodule
